// Logisim project Logisim.circ as structural Verilog: 3 circuits, main circuit Guia_0701
module Guia_0701 (
  input  in_1,
  input  in_2,
  input  Chave,
  output out_4
);

  wire and_1_out, and_2_out, and_3_out, and_4_out, not_1_out, not_2_out;

  and and_1 (and_1_out, in_1, in_2);
  and and_2 (and_2_out, in_1, in_2);
  not not_1 (not_1_out, and_2_out);
  not not_2 (not_2_out, Chave);
  and and_3 (and_3_out, and_1_out, not_2_out);
  and and_4 (and_4_out, Chave, not_1_out);
  or or_1 (out_4, and_3_out, and_4_out);

  // Notes on the sheet:
  //   AND
  //   NAND
  //   Mux
endmodule

module Guia_0702 (
  input  in_1,
  input  in_2,
  input  Chave,
  output out_4
);

  wire and_1_out, and_2_out, not_1_out, not_2_out, or_1_out, or_2_out;

  or or_1 (or_1_out, in_1, in_2);
  or or_2 (or_2_out, in_1, in_2);
  not not_1 (not_1_out, or_2_out);
  not not_2 (not_2_out, Chave);
  and and_1 (and_1_out, or_1_out, not_2_out);
  and and_2 (and_2_out, Chave, not_1_out);
  or or_3 (out_4, and_1_out, and_2_out);

  // Notes on the sheet:
  //   OR
  //   NOR
  //   Mux
endmodule

module Guia_0703 (
  input  Chave,
  input  in_2,
  input  in_3,
  input  in_4,
  input  Chave_2,
  input  in_6,
  output out_7
);

  wire and_1_out, and_2_out, and_3_out, and_4_out, and_5_out, and_6_out, and_7_out, and_8_out, not_1_out,
       not_2_out, not_3_out, not_4_out, not_5_out, or_1_out, or_2_out, or_3_out, or_4_out;

  and and_1 (and_1_out, in_2, in_3);
  not not_1 (not_1_out, and_2_out);
  and and_2 (and_2_out, in_2, in_3);
  or or_1 (or_1_out, in_4, in_6);
  or or_2 (or_2_out, in_4, in_6);
  not not_2 (not_2_out, or_2_out);
  not not_3 (not_3_out, Chave);
  not not_4 (not_4_out, Chave);
  and and_3 (and_3_out, and_1_out, not_3_out);
  and and_4 (and_4_out, Chave, not_1_out);
  and and_5 (and_5_out, or_1_out, not_4_out);
  and and_6 (and_6_out, Chave, not_2_out);
  or or_3 (or_3_out, and_3_out, and_4_out);
  or or_4 (or_4_out, and_5_out, and_6_out);
  not not_5 (not_5_out, Chave_2);
  and and_7 (and_7_out, or_3_out, not_5_out);
  and and_8 (and_8_out, Chave_2, or_4_out);
  or or_5 (out_7, and_7_out, and_8_out);

  // Notes on the sheet:
  //   AND
  //   NAND
  //   OR
  //   NOR
  //   Mux
  //   Mux
  //   Mux
endmodule
