// Logisim project somadores.circ as structural Verilog
module meia_soma (
  input  x0,
  input  y0,
  output s0,
  output Carry_Out
);

  xor xor_1 (s0, x0, y0);
  and and_1 (Carry_Out, y0, x0);
endmodule

module soma_completa (
  input  Vem1,
  input  x1,
  input  y1,
  output out_4,
  output out_5
);

  wire meia_soma_1_carry_out, meia_soma_1_s0, meia_soma_2_carry_out;

  meia_soma meia_soma_1 (.x0(x1), .y0(y1), .s0(meia_soma_1_s0), .Carry_Out(meia_soma_1_carry_out));
  meia_soma meia_soma_2 (.x0(Vem1), .y0(meia_soma_1_s0), .s0(out_4), .Carry_Out(meia_soma_2_carry_out));
  or or_1 (out_5, meia_soma_1_carry_out, meia_soma_2_carry_out);
endmodule

module soma_4bits (
  input  x0,
  input  y0,
  input  x1,
  input  y1,
  input  x2,
  input  y2,
  input  x3,
  input  y3,
  output out_9,
  output out_10,
  output out_11,
  output out_12,
  output out_13
);

  wire soma_completa_1_out_5, soma_completa_2_out_5, soma_completa_3_out_5;

  soma_completa soma_completa_1 (.x1(x0), .y1(y0), .Vem1(1'b0), .out_5(soma_completa_1_out_5), .out_4(out_9));
  soma_completa soma_completa_2 (
    .x1(x1), .y1(y1), .Vem1(soma_completa_1_out_5), .out_5(soma_completa_2_out_5), .out_4(out_10));
  soma_completa soma_completa_3 (
    .x1(x2), .y1(y2), .Vem1(soma_completa_2_out_5), .out_5(soma_completa_3_out_5), .out_4(out_11));
  soma_completa soma_completa_4 (.x1(x3), .y1(y3), .Vem1(soma_completa_3_out_5), .out_5(out_13), .out_4(out_12));
endmodule
